# Fritzing sketch sketch (saved by Fritzing 0.9.3b)
breadboards: 2

parts:
  U1 = NodeMCU V1.0
  LED1 = smd LED [color="Red (633nm)" package="0603 [SMD]"]
  R1 = Resistor [tolerance=±5% resistance=22 package="0603 [SMD]"]

nets:
  N1: U1.GND, LED1.cathode
  N2: U1.D6, R1.Pin_1
  N3: LED1.anode, R1.Pin_0

custom parts:
  NodeMCU V1.0: ESP8266 based NodeMCU
