# Fritzing sketch sketch (saved by Fritzing 0.9.3b)
breadboards: 1

parts:
  U1 = NodeMCU V1.0
  R1 = Resistor [tolerance=±5% resistance=20 package="0603 [SMD]"]
  LED3 = RGB LED - (4 legs) [package="5 mm [THT]"]
  R2 = Resistor [tolerance=±5% resistance=20 package="0603 [SMD]"]
  R3 = Resistor [tolerance=±5% resistance=60 package="0603 [SMD]"]

nets:
  N1: U1.3V3, LED3.common_anode
  N2: U1.D5, R3.Pin_1
  N3: U1.D6, R2.Pin_1
  N4: U1.D7, R1.Pin_1
  N5: R1.Pin_0, LED3.blue_cathode
  N6: LED3.red_cathode, R3.Pin_0
  N7: LED3.green_cathode, R2.Pin_0

custom parts:
  NodeMCU V1.0: ESP8266 based NodeMCU
