# Fritzing sketch sketch (saved by Fritzing 0.9.3b)
breadboards: 1

parts:
  U1 = NodeMCU V1.0
  S1 = Pushbutton [package="[SMD]"]
  S2 = Pushbutton [package="[SMD]"]
  R1 = Resistor [tolerance=±5% resistance=100 package="0603 [SMD]"]
  R2 = Resistor [tolerance=±5% resistance=100 package="0603 [SMD]"]

nets:
  N1: U1.D1, S2.Pin_3, S2.Pin_4, R1.Pin_1
  N2: U1.D2, S1.Pin_3, S1.Pin_4, R2.Pin_1
  N3: U1.3V3, S1.Pin_1, S1.Pin_2, S2.Pin_1, S2.Pin_2
  N4: U1.GND, R1.Pin_0, R2.Pin_0

custom parts:
  NodeMCU V1.0: ESP8266 based NodeMCU

// code stored in the sketch: Untitled5.ino

